// Logisim project Cache.circ as structural Verilog: 6 circuits, main circuit main
module main (
  input  in_1,
  input  [7:0] Fetched_Instruction,
  input  [7:0] Data,
  output [15:0] PC_Address,
  output [15:0] Mem_Address
);

  wire [7:0] decode_1_out_2, decode_2_out_2, decode_4_out_2, register_1_q, register_2_q, register_3_q,
       register_4_q;

  Counter #(.width(16), .max('hffff)) PC (
    .Q(PC_Address), .clk(in_1));  // open: load, D, count, carry, clr, preset, down
  Register #(.Select("low")) register_1 (.D(Fetched_Instruction), .Q(register_1_q), .clk(in_1));  // open: en, clr
  Decode decode_1 (.in_1(register_1_q), .out_2(decode_1_out_2));
  Register #(.Select("low")) register_2 (.D(decode_1_out_2), .Q(register_2_q), .clk(in_1));  // open: en, clr
  Decode decode_2 (.in_1(register_2_q), .out_2(decode_2_out_2));
  Register #(.Select("low")) register_3 (.D(decode_2_out_2), .Q(register_3_q), .clk(in_1));  // open: en, clr
  Decode decode_3 (.in_1(register_3_q), .out_2(Mem_Address[7:0]));
  Register #(.Select("low")) register_4 (.D(Data), .Q(register_4_q), .clk(in_1));  // open: en, clr
  Decode decode_4 (.in_1(register_4_q), .out_2(decode_4_out_2));
  Register #(.Select("low")) register_5 (.D(decode_4_out_2), .clk(in_1));  // open: en, Q, clr

  assign Mem_Address[15:8] = {8{1'b0}};

  // Other names for the same wires on the sheet: clk = in_1
endmodule

module Decode (
  input  [7:0] in_1,
  output [7:0] out_2
);

  Multiplier multiplier_1 (.a(in_1), .b(8'h2), .out(out_2));  // open: cin, cout
endmodule

module RAM (
  input  [15:0] MP_Addr,
  input  [7:0] in_2,
  input  in_3,
  input  in_4,
  input  in_5,
  output [7:0] MP_DataOut
);

  RAM_part #(.addrWidth(16), .bus("separate"), .Select("low")) ram_1 (
    .addr(MP_Addr), .din(in_2), .data(MP_DataOut), .str(in_4), .sel(1'b0), .clk(in_5), .ld(in_3));  // open: clr

  // Other names for the same wires on the sheet: clk = in_5; MP_Ld = in_3; MP_Str = in_4

  // Notes on the sheet:
  //   MP_DataIn
endmodule

module MAIN (
  input  [7:0] Fetched_Instruction,
  input  [7:0] Data,
  input  [15:0] in_3,
  input  in_4,
  input  in_5,
  input  in_6,
  output [15:0] PC_Address,
  output [15:0] Mem_Address
);

  wire clk, comparator_1_eq, comparator_2_eq, comparator_3_eq, demultiplexer_2_out0, demultiplexer_2_out1,
       demultiplexer_2_out2, demultiplexer_2_out3, demultiplexer_2_out4, demultiplexer_2_out5,
       demultiplexer_2_out6, demultiplexer_2_out7, I_L2_Request, IF_Enable, L1_I_Hit, L1_I_Valid_RAM_data,
       L1_I_WriteTag, L1_LoadLine, L2_Miss, L2_Tag_RAM_data, L2_Valid_RAM_data, not_2_out, not_4_out;
  wire [1:0] counter_2_q;
  wire [2:0] counter_3_q;
  wire [3:0] L1_I_Tag_RAM_data;
  wire [7:0] decode_1_out_2, decode_2_out_2, decode_4_out_2, demultiplexer_1_out0, demultiplexer_1_out1,
       demultiplexer_1_out2, demultiplexer_1_out3, InstFinal_I, L1_I_SelectedByte, L2_SelectedByte,
       ram_2_data, register_1_q, register_2_q, register_3_q, register_4_q, register_5_q, register_6_q,
       register_7_q, register_8_q, register_9_q, register_10_q;
  wire [15:0] counter_1_q, MP_Addr;
  wire [31:0] L1_DataOut_0, L1_DataOut_1, L2_DataOut_0_31__0, L2_DataOut_1_31__0, L2_DataOut_2_31__0,
       L2_DataOut_3_31__0, L2_DataOut_4_31__0, L2_DataOut_5_31__0, L2_DataOut_6_31__0, L2_DataOut_7_31__0,
       L2_SubBlock64_31__0, L2_SubBlock64_63__32;

  main main_1 (.in_1(clk));  // open: Fetched_Instruction, Data, PC_Address, Mem_Address
  RAM ram_1 ();  // open: in_2, MP_Addr, in_5, in_3, in_4, MP_DataOut
  L2 l2_1 (.in_1(clk));  // open: in_2, in_3, in_4, in_5, in_6, in_14, in_11, in_12, in_13, in_7, in_8, in_9, in_10, L2_SelectedByte_7__0, out_16, out_17
  Clock clock_1 (.out(clk));
  Counter #(.width(16), .max('h1f)) counter_1 (
    .count(L2_Miss), .Q(counter_1_q), .clk(clk), .clr(L1_I_WriteTag));  // open: load, D, carry, preset, down
  Adder #(.width(16)) adder_1 (.a({in_3[15:5], {5{1'b0}}}), .b(counter_1_q), .out(MP_Addr));  // open: cin, cout
  Counter #(.width(16), .max('hffff)) PC (
    .count(IF_Enable), .Q(PC_Address), .clk(clk));  // open: load, D, carry, clr, preset, down
  Register #(.Select("low")) register_1 (
    .D(Fetched_Instruction), .en(IF_Enable), .Q(register_1_q), .clk(clk));  // open: clr
  not not_1 (IF_Enable, I_L2_Request);
  RAM_part #(.addrWidth(16), .bus("separate"), .Select("low")) ram_2 (
    .addr(MP_Addr), .data(ram_2_data), .sel(1'b0), .clk(clk), .ld(L2_Miss));  // open: din, str, clr
  Decode decode_1 (.in_1(register_1_q), .out_2(decode_1_out_2));
  Comparator #(.width(1)) comparator_1 (.a(L2_Tag_RAM_data), .b(in_3[15]), .eq(comparator_1_eq));  // open: gt, lt
  Register #(.Select("low")) register_2 (.D(decode_1_out_2), .Q(register_2_q), .clk(clk));  // open: en, clr
  Decode decode_2 (.in_1(register_2_q), .out_2(decode_2_out_2));
  Multiplexer #(.select(3), .width(8), .enable("false")) multiplexer_1 (
    .in0(L1_DataOut_0[7:0]), .in1(L1_DataOut_0[15:8]), .in2(L1_DataOut_0[23:16]), .in3(L1_DataOut_0[31:24]),
    .in4(L1_DataOut_1[7:0]), .in5(L1_DataOut_1[15:8]), .in6(L1_DataOut_1[23:16]), .in7(L1_DataOut_1[31:24]),
    .out(L1_I_SelectedByte), .sel(in_3[2:0]));
  RAM_part #(.addrWidth(9), .dataWidth(4), .bus("separate"), .Select("low")) L1_I_Tag_RAM (
    .addr(in_3[11:3]), .din(in_3[15:12]), .data(L1_I_Tag_RAM_data), .str(L1_I_WriteTag), .sel(1'b0),
    .clk(clk), .ld(1'b1));  // open: clr
  and and_1 (L1_I_WriteTag, L2_Valid_RAM_data, I_L2_Request, comparator_1_eq);
  Demultiplexer #(.select(2), .width(8), .enable("false")) demultiplexer_1 (
    .out0(demultiplexer_1_out0), .out1(demultiplexer_1_out1), .out2(demultiplexer_1_out2),
    .out3(demultiplexer_1_out3), .in(ram_2_data), .sel(counter_2_q));
  Counter #(.width(2), .max('h3)) counter_2 (
    .count(L2_Miss), .Q(counter_2_q), .clk(clk), .clr(L1_I_WriteTag));  // open: load, D, carry, preset, down
  Decode decode_3 (.in_1(register_3_q), .out_2(Mem_Address[7:0]));
  Register #(.Select("low")) register_3 (.D(decode_2_out_2), .Q(register_3_q), .clk(clk));  // open: en, clr
  Comparator #(.width(4)) comparator_2 (.a(L1_I_Tag_RAM_data), .b(in_3[15:12]), .eq(comparator_2_eq));  // open: gt, lt
  Multiplexer #(.select(2), .width(32), .enable("false")) multiplexer_2 (
    .in0(L2_DataOut_0_31__0), .in1(L2_DataOut_2_31__0), .in2(L2_DataOut_4_31__0), .in3(L2_DataOut_6_31__0),
    .out(L2_SubBlock64_31__0), .sel(in_3[4:3]));
  Multiplexer #(.select(2), .width(32), .enable("false")) multiplexer_3 (
    .in0(L2_DataOut_1_31__0), .in1(L2_DataOut_3_31__0), .in3(L2_DataOut_5_31__0), .out(L2_SubBlock64_63__32),
    .sel(in_3[4:3]));  // open: in2
  RAM_part #(.addrWidth(10), .dataWidth(1), .bus("separate"), .Select("low")) L2_Tag_RAM (
    .addr(in_3[14:5]), .din(in_3[15]), .data(L2_Tag_RAM_data), .str(in_4), .sel(1'b0), .clk(clk),
    .ld(I_L2_Request));  // open: clr
  not not_2 (not_2_out, L1_I_WriteTag);
  Register #(.Select("low")) register_4 (.D(demultiplexer_1_out0), .Q(register_4_q), .clk(clk));  // open: en, clr
  Register #(.Select("low")) register_5 (.D(demultiplexer_1_out1), .Q(register_5_q), .clk(clk));  // open: en, clr
  Register #(.Select("low")) register_6 (.D(demultiplexer_1_out2), .Q(register_6_q), .clk(clk));  // open: en, clr
  Comparator #(.width(2)) comparator_3 (.a(counter_2_q), .b(2'b11), .eq(comparator_3_eq));  // open: gt, lt
  Register #(.Select("low")) register_7 (.D(register_8_q), .Q(register_7_q), .clk(clk));  // open: en, clr
  Register #(.Select("low")) register_8 (.D(register_4_q), .Q(register_8_q), .clk(clk));  // open: en, clr
  Register #(.Select("low")) register_9 (.D(register_5_q), .Q(register_9_q), .clk(clk));  // open: en, clr
  Counter #(.width(3), .max('h7)) counter_3 (
    .count(comparator_3_eq), .Q(counter_3_q), .clk(clk));  // open: load, D, carry, clr, preset, down
  Demultiplexer #(.select(3), .enable("false")) demultiplexer_2 (
    .out0(demultiplexer_2_out0), .out1(demultiplexer_2_out1), .out2(demultiplexer_2_out2),
    .out3(demultiplexer_2_out3), .out4(demultiplexer_2_out4), .out5(demultiplexer_2_out5),
    .out6(demultiplexer_2_out6), .out7(demultiplexer_2_out7), .in(1'b1), .sel(counter_3_q));
  Register #(.Select("low")) register_10 (.D(Data), .Q(register_10_q), .clk(clk));  // open: en, clr
  RAM_part #(.addrWidth(9), .dataWidth(1), .bus("separate"), .Select("low")) L1_I_Valid_RAM (
    .addr(in_3[11:3]), .din(1'b1), .data(L1_I_Valid_RAM_data), .str(L1_I_WriteTag), .sel(1'b0), .clk(clk),
    .ld(1'b1));  // open: clr
  Multiplexer #(.select(3), .width(8), .enable("false")) multiplexer_4 (
    .in0(L2_SubBlock64_31__0[7:0]), .in1(L2_SubBlock64_31__0[15:8]), .in2(L2_SubBlock64_31__0[23:16]),
    .in3(L2_SubBlock64_31__0[31:24]), .in4(L2_SubBlock64_63__32[7:0]), .in5(L2_SubBlock64_63__32[15:8]),
    .in6(L2_SubBlock64_63__32[23:16]), .in7(L2_SubBlock64_63__32[31:24]), .out(L2_SelectedByte), .sel(3'b000));
  and and_2 (L2_Miss, not_2_out, I_L2_Request);
  Decode decode_4 (.in_1(register_10_q), .out_2(decode_4_out_2));
  and and_3 (L1_I_Hit, L1_I_Valid_RAM_data, comparator_2_eq);
  RAM_part #(.addrWidth(10), .dataWidth(1), .bus("separate"), .Select("low")) L2_Valid_RAM (
    .addr(in_3[14:5]), .din(1'b1), .data(L2_Valid_RAM_data), .str(in_5), .sel(1'b0), .clk(clk),
    .ld(I_L2_Request));  // open: clr
  Register #(.Select("low")) register_11 (.D(decode_4_out_2), .clk(clk));  // open: en, Q, clr
  not not_3 (I_L2_Request, L1_I_Hit);
  RAM_part #(.addrWidth(9), .dataWidth(32), .bus("separate"), .Select("low")) L1_I_Data_RAM_0 (
    .addr(in_3[11:3]), .din(L2_SubBlock64_31__0), .data(L1_DataOut_0), .str(L1_I_WriteTag), .sel(1'b0),
    .clk(clk), .ld(1'b1), .clr(L1_LoadLine));
  not not_4 (not_4_out, L1_I_Hit);
  RAM_part #(.addrWidth(10), .dataWidth(32), .bus("separate"), .Select("low")) L2_Data_RAM_0 (
    .addr(in_3[14:5]), .din({demultiplexer_1_out3, register_6_q, register_9_q, register_7_q}),
    .data(L2_DataOut_0_31__0), .str(demultiplexer_2_out0), .sel(1'b0), .clk(clk), .ld(1'b1));  // open: clr
  Multiplexer #(.width(8), .enable("false")) multiplexer_5 (
    .in0(L1_I_SelectedByte), .in1(L2_SelectedByte), .out(InstFinal_I), .sel(not_4_out));
  RAM_part #(.addrWidth(9), .dataWidth(32), .bus("separate"), .Select("low")) L1_I_Data_RAM_1 (
    .addr(in_3[11:3]), .din(L2_SubBlock64_63__32), .data(L1_DataOut_1), .str(L1_I_WriteTag), .sel(1'b0),
    .clk(clk), .ld(1'b1), .clr(L1_LoadLine));
  RAM_part #(.addrWidth(10), .dataWidth(32), .bus("separate"), .Select("low")) L2_Data_RAM_1 (
    .addr(in_3[14:5]), .din({demultiplexer_1_out3, register_6_q, register_9_q, register_7_q}),
    .data(L2_DataOut_1_31__0), .str(demultiplexer_2_out1), .sel(1'b0), .clk(clk), .ld(1'b1));  // open: clr
  RAM_part #(.addrWidth(10), .dataWidth(32), .bus("separate"), .Select("low")) L2_Data_RAM_2 (
    .addr(in_3[14:5]), .din({demultiplexer_1_out3, register_6_q, register_9_q, register_7_q}),
    .data(L2_DataOut_2_31__0), .str(demultiplexer_2_out2), .sel(1'b0), .clk(clk), .ld(1'b1));  // open: clr
  RAM_part #(.addrWidth(10), .dataWidth(32), .bus("separate"), .Select("low")) L2_Data_RAM_3 (
    .addr(in_3[14:5]), .din({demultiplexer_1_out3, register_6_q, register_9_q, register_7_q}),
    .data(L2_DataOut_3_31__0), .str(demultiplexer_2_out3), .sel(1'b0), .clk(clk), .ld(1'b1));  // open: clr
  RAM_part #(.addrWidth(10), .dataWidth(32), .bus("separate"), .Select("low")) L2_Data_RAM_4 (
    .addr(in_3[14:5]), .din({demultiplexer_1_out3, register_6_q, register_9_q, register_7_q}),
    .data(L2_DataOut_4_31__0), .str(demultiplexer_2_out4), .sel(1'b0), .clk(clk), .ld(1'b1));  // open: clr
  RAM_part #(.addrWidth(10), .dataWidth(32), .bus("separate"), .Select("low")) L2_Data_RAM_5 (
    .addr(in_3[14:5]), .din({demultiplexer_1_out3, register_6_q, register_9_q, register_7_q}),
    .data(L2_DataOut_5_31__0), .str(demultiplexer_2_out5), .sel(1'b0), .clk(clk), .ld(1'b1));  // open: clr
  RAM_part #(.addrWidth(10), .dataWidth(32), .bus("separate"), .Select("low")) L2_Data_RAM_6 (
    .addr(in_3[14:5]), .din({demultiplexer_1_out3, register_6_q, register_9_q, register_7_q}),
    .data(L2_DataOut_6_31__0), .str(demultiplexer_2_out6), .sel(1'b0), .clk(clk), .ld(1'b1));  // open: clr
  RAM_part #(.addrWidth(10), .dataWidth(32), .bus("separate"), .Select("low")) L2_Data_RAM_7 (
    .addr(in_3[14:5]), .din({demultiplexer_1_out3, register_6_q, register_9_q, register_7_q}),
    .data(L2_DataOut_7_31__0), .str(demultiplexer_2_out7), .sel(1'b0), .clk(clk), .ld(1'b1));  // open: clr

  assign Mem_Address[15:8] = {8{1'b0}};

  // Other names for the same wires on the sheet: L1_I_Addr[15:0] = in_3; L1_I_Offset[2:0] = in_3[2:0];
  //   L1_I_Index[8:0] = in_3[11:3]; L2_Addr[15:3] = in_3[15:3]; L2_Offset[4:3] = in_3[4:3];
  //   L2_Index[9:0] = in_3[14:5]; L1_I_Tag[3:0] = in_3[15:12]; L2_Tag = in_3[15]; L1_I_Miss = I_L2_Request;
  //   L1_I_WriteValid = L1_I_WriteTag; L1_WriteData = L1_I_WriteTag; L2_Hit = L1_I_WriteTag; L2_LoadLine = in_6;
  //   L2_WriteTag = in_4; L2_WriteValid = in_5; MP_Ld = L2_Miss

  // Notes on the sheet:
  //   L2_TagMatch
  //   L1_I_StoredTag
  //   L2_StoredTag
  //   L1_I_Valid
  //   L2_Valid
endmodule

module L2 (
  input  in_1,
  input  [15:0] in_2,
  input  in_3,
  input  in_4,
  input  in_5,
  input  in_6,
  input  [31:0] in_7,
  input  [31:0] in_8,
  input  [31:0] in_9,
  input  [31:0] in_10,
  input  [31:0] in_11,
  input  [31:0] in_12,
  input  [31:0] in_13,
  input  [31:0] in_14,
  output [7:0] L2_SelectedByte_7__0,
  output out_16,
  output out_17
);

  wire comparator_1_eq, L2_Tag_RAM_data, L2_Valid_RAM_data;
  wire [31:0] L2_DataOut_0_31__0, L2_DataOut_1_31__0, L2_DataOut_2_31__0, L2_DataOut_3_31__0,
       L2_DataOut_4_31__0, L2_DataOut_5_31__0, L2_DataOut_6_31__0, L2_DataOut_7_31__0, multiplexer_1_out,
       multiplexer_2_out;

  Toy_model toy_model_1 ();
  RAM_part #(.addrWidth(10), .dataWidth(1), .bus("separate"), .Select("low")) L2_Tag_RAM (
    .addr(in_2[14:5]), .din(in_2[15]), .data(L2_Tag_RAM_data), .str(in_3), .sel(1'b0), .clk(in_1), .ld(1'b1));  // open: clr
  Comparator #(.width(1)) comparator_1 (.a(L2_Tag_RAM_data), .b(in_2[15]), .eq(comparator_1_eq));  // open: gt, lt
  Multiplexer #(.select(2), .width(32), .enable("false")) multiplexer_1 (
    .in0(L2_DataOut_0_31__0), .in1(L2_DataOut_2_31__0), .in2(L2_DataOut_4_31__0), .in3(L2_DataOut_6_31__0),
    .out(multiplexer_1_out), .sel(in_2[4:3]));
  Multiplexer #(.select(2), .width(32), .enable("false")) multiplexer_2 (
    .in0(L2_DataOut_1_31__0), .in1(L2_DataOut_3_31__0), .in3(L2_DataOut_5_31__0), .out(multiplexer_2_out),
    .sel(in_2[4:3]));  // open: in2
  RAM_part #(.addrWidth(10), .dataWidth(1), .bus("separate"), .Select("low")) L2_Valid_RAM (
    .addr(in_2[14:5]), .din(1'b1), .data(L2_Valid_RAM_data), .str(in_4), .sel(1'b0), .clk(in_1), .ld(1'b1));  // open: clr
  and and_1 (out_16, L2_Valid_RAM_data, comparator_1_eq);
  Multiplexer #(.select(3), .width(8), .enable("false")) multiplexer_3 (
    .in0(multiplexer_1_out[7:0]), .in1(multiplexer_1_out[15:8]), .in2(multiplexer_1_out[23:16]),
    .in3(multiplexer_1_out[31:24]), .in4(multiplexer_2_out[7:0]), .in5(multiplexer_2_out[15:8]),
    .in6(multiplexer_2_out[23:16]), .in7(multiplexer_2_out[31:24]), .out(L2_SelectedByte_7__0),
    .sel(in_2[2:0]));
  not not_1 (out_17, out_16);
  RAM_part #(.addrWidth(10), .dataWidth(32), .bus("separate"), .Select("low")) L2_Data_RAM_0 (
    .addr(in_2[14:5]), .din(in_7), .data(L2_DataOut_0_31__0), .str(in_5), .sel(1'b0), .clk(in_1), .ld(1'b1),
    .clr(in_6));
  RAM_part #(.addrWidth(10), .dataWidth(32), .bus("separate"), .Select("low")) L2_Data_RAM_1 (
    .addr(in_2[14:5]), .din(in_8), .data(L2_DataOut_1_31__0), .str(in_5), .sel(1'b0), .clk(in_1), .ld(1'b1),
    .clr(in_6));
  RAM_part #(.addrWidth(10), .dataWidth(32), .bus("separate"), .Select("low")) L2_Data_RAM_2 (
    .addr(in_2[14:5]), .din(in_9), .data(L2_DataOut_2_31__0), .str(in_5), .sel(1'b0), .clk(in_1), .ld(1'b1),
    .clr(in_6));
  RAM_part #(.addrWidth(10), .dataWidth(32), .bus("separate"), .Select("low")) L2_Data_RAM_3 (
    .addr(in_2[14:5]), .din(in_10), .data(L2_DataOut_3_31__0), .str(in_5), .sel(1'b0), .clk(in_1), .ld(1'b1),
    .clr(in_6));
  RAM_part #(.addrWidth(10), .dataWidth(32), .bus("separate"), .Select("low")) L2_Data_RAM_4 (
    .addr(in_2[14:5]), .din(in_11), .data(L2_DataOut_4_31__0), .str(in_5), .sel(1'b0), .clk(in_1), .ld(1'b1),
    .clr(in_6));
  RAM_part #(.addrWidth(10), .dataWidth(32), .bus("separate"), .Select("low")) L2_Data_RAM_5 (
    .addr(in_2[14:5]), .din(in_12), .data(L2_DataOut_5_31__0), .str(in_5), .sel(1'b0), .clk(in_1), .ld(1'b1),
    .clr(in_6));
  RAM_part #(.addrWidth(10), .dataWidth(32), .bus("separate"), .Select("low")) L2_Data_RAM_6 (
    .addr(in_2[14:5]), .din(in_13), .data(L2_DataOut_6_31__0), .str(in_5), .sel(1'b0), .clk(in_1), .ld(1'b1),
    .clr(in_6));
  RAM_part #(.addrWidth(10), .dataWidth(32), .bus("separate"), .Select("low")) L2_Data_RAM_7 (
    .addr(in_2[14:5]), .din(in_14), .data(L2_DataOut_7_31__0), .str(in_5), .sel(1'b0), .clk(in_1), .ld(1'b1),
    .clr(in_6));

  // Other names for the same wires on the sheet: clk = in_1; L2_DataIn_0_31__0[31:0] = in_7;
  //   L2_DataIn_1_31__0[31:0] = in_8; L2_DataIn_2_31__0[31:0] = in_9; L2_DataIn_3_31__0[31:0] = in_10;
  //   L2_DataIn_4_31__0[31:0] = in_11; L2_DataIn_5_31__0[31:0] = in_12; L2_DataIn_6_31__0[31:0] = in_13;
  //   L2_DataIn_7_31__0[31:0] = in_14; L2_LoadLine = in_6; L2_WriteData = in_5; L2_WriteTag = in_3;
  //   L2_WriteValid = in_4

  // Notes on the sheet:
  //   L2_Offset
  //   L2_Index
  //   L2_Tag
  //   L2_Tag
  //   L2_StoredTag
  //   L2_TagMatch
  //   L2_Valid
  //   L2_Hit
  //   L2_Miss
endmodule

module Toy_model (
);

  wire and_1_out, clk, comparator_1_eq, comparator_2_eq, comparator_3_eq, I_L2_Request, L2_Hit, not_1_out,
       not_3_out, ram_2_data, ram_5_data;
  wire [1:0] counter_2_q;
  wire [3:0] ram_4_data;
  wire [4:0] ram_1_data;
  wire [7:0] counter_1_q, demultiplexer_1_out0, demultiplexer_1_out1, demultiplexer_1_out2,
       multiplexer_1_out, multiplexer_2_out, multiplexer_4_out, ram_6_data, register_2_q, register_3_q,
       register_4_q;
  wire [15:0] multiplexer_3_out, ram_3_data;
  wire [31:0] ram_7_data, register_7_q;

  Clock clock_1 (.out(clk));
  Counter counter_1 (.count(not_1_out), .Q(counter_1_q), .clk(clk));  // open: load, D, carry, clr, preset, down
  not not_1 (not_1_out, I_L2_Request);
  Comparator #(.width(5)) comparator_1 (.a(ram_1_data), .b(counter_1_q[7:3]), .eq(comparator_1_eq));  // open: gt, lt
  RAM_part #(.addrWidth(2), .dataWidth(5), .bus("separate"), .Select("low")) ram_1 (
    .addr(counter_1_q[2:1]), .din(counter_1_q[7:3]), .data(ram_1_data), .str(L2_Hit), .sel(1'b0), .clk(clk),
    .ld(1'b1));  // open: clr
  and and_1 (and_1_out, ram_2_data, comparator_1_eq);
  not not_2 (I_L2_Request, and_1_out);
  RAM_part #(.addrWidth(2), .dataWidth(1), .bus("separate"), .Select("low")) ram_2 (
    .addr(counter_1_q[2:1]), .din(1'b1), .data(ram_2_data), .str(L2_Hit), .sel(1'b0), .clk(clk), .ld(1'b1));  // open: clr
  RAM_part #(.addrWidth(2), .dataWidth(16), .bus("separate"), .Select("low")) ram_3 (
    .addr(counter_1_q[2:1]), .din(multiplexer_3_out), .data(ram_3_data), .str(L2_Hit), .sel(1'b0), .clk(clk),
    .ld(1'b1));  // open: clr
  Comparator #(.width(4)) comparator_2 (.a(ram_4_data), .b(counter_1_q[7:4]), .eq(comparator_2_eq));  // open: gt, lt
  Multiplexer #(.width(8), .enable("false")) multiplexer_1 (
    .in0(ram_3_data[7:0]), .in1(ram_3_data[15:8]), .out(multiplexer_1_out), .sel(counter_1_q[0]));
  RAM_part #(.addrWidth(2), .dataWidth(4), .bus("separate"), .Select("low")) ram_4 (
    .addr(counter_1_q[3:2]), .din(counter_1_q[7:4]), .data(ram_4_data), .str(comparator_3_eq), .sel(1'b0),
    .clk(clk), .ld(I_L2_Request));  // open: clr
  and and_2 (L2_Hit, ram_5_data, comparator_2_eq);
  not not_3 (not_3_out, L2_Hit);
  Multiplexer #(.width(8), .enable("false")) multiplexer_2 (
    .in0(multiplexer_1_out), .in1(multiplexer_4_out), .out(multiplexer_2_out), .sel(and_1_out));
  Register #(.Select("low")) register_1 (.D(multiplexer_2_out), .clk(clk));  // open: en, Q, clr
  RAM_part #(.addrWidth(2), .dataWidth(1), .bus("separate"), .Select("low")) ram_5 (
    .addr(counter_1_q[3:2]), .din(1'b1), .data(ram_5_data), .str(comparator_3_eq), .sel(1'b0), .clk(clk),
    .ld(I_L2_Request));  // open: clr
  RAM_part #(.bus("separate"), .Select("low")) ram_6 (
    .addr({counter_1_q[7:2], 2'b00}), .data(ram_6_data), .sel(1'b0), .clk(clk), .ld(not_3_out));  // open: din, str, clr
  Demultiplexer #(.select(2), .width(8), .enable("false")) demultiplexer_1 (
    .out0(demultiplexer_1_out0), .out1(demultiplexer_1_out1), .out2(demultiplexer_1_out2),
    .out3(register_7_q[31:24]), .in(ram_6_data), .sel(counter_2_q));
  Counter #(.width(2), .max('h3)) counter_2 (
    .count(not_3_out), .Q(counter_2_q), .clk(clk));  // open: load, D, carry, clr, preset, down
  RAM_part #(.addrWidth(2), .dataWidth(32), .bus("separate"), .Select("low")) ram_7 (
    .addr(counter_1_q[3:2]), .din(register_7_q), .data(ram_7_data), .str(comparator_3_eq), .sel(1'b0),
    .clk(clk), .ld(I_L2_Request));  // open: clr
  Register #(.Select("low")) register_2 (.D(register_3_q), .Q(register_2_q), .clk(clk));  // open: en, clr
  Register #(.Select("low")) register_3 (.D(demultiplexer_1_out0), .Q(register_3_q), .clk(clk));  // open: en, clr
  Register #(.Select("low")) register_4 (.D(demultiplexer_1_out1), .Q(register_4_q), .clk(clk));  // open: en, clr
  Register #(.Select("low")) register_5 (.D(register_4_q), .Q(register_7_q[15:8]), .clk(clk));  // open: en, clr
  Register #(.Select("low")) register_6 (
    .D(demultiplexer_1_out2), .Q(register_7_q[23:16]), .clk(clk));  // open: en, clr
  Comparator #(.width(2)) comparator_3 (.a(counter_2_q), .b(2'b11), .eq(comparator_3_eq));  // open: gt, lt
  Register #(.Select("low")) register_7 (.D(register_2_q), .Q(register_7_q[7:0]), .clk(clk));  // open: en, clr
  Multiplexer #(.width(16), .enable("false")) multiplexer_3 (
    .in0(ram_7_data[15:0]), .in1(ram_7_data[31:16]), .out(multiplexer_3_out), .sel(counter_1_q[1]));
  Multiplexer #(.width(8), .enable("false")) multiplexer_4 (
    .in0(multiplexer_3_out[7:0]), .in1(multiplexer_3_out[15:8]), .out(multiplexer_4_out), .sel(1'b0));

  // Notes on the sheet:
  //   Brandon Trigueros Lara
  //   David González Villanueva
  //   Milton Sojo Córdoba
  //   Stall PC
  //   I_Offset[0]
  //   I_Index[1..0]
  //   I_Tag[4..0]
  //   I_L1_WriteTag
  //   I_TagMatch
  //   I_StoredTag[4..0]
  //   I_L1_WriteValid
  //   I_L1_Hit
  //   I_L1_Miss
  //   I_L2_Request
  //   I_Valid[0]
  //   I_BlockIn[15..0]
  //   I_L1_WriteData
  //   L2_Offset[1..0]
  //   L2_Index[1..0]
  //   L2_Tag[3..0]
  //   I_BlockOut[15..0]
  //   I_Byte0
  //   I_Byte1 
  //   L2_WriteTag
  //   L2_TagMatch
  //   I_ByteFromL1[7..0]
  //   L2_StoredTag[3..0]  
  //   L2_Hit
  //   L2_WriteValid
  //   L2_Miss
  //   InstFinal_I[7..0]
  //   MP_Addr[7..0]
  //   L2_Valid[0] 
  //   MP_Ld
  //   L2_WriteData
  //   MP_DataOut[7..0]
  //   L2_BlockOut[31..0]  
  //   L2_SelectedByte[7..0]
endmodule
