// Logisim project cpu4bits.circ as structural Verilog: 1 circuit, main circuit main
module main (
  input  in_1
);

  wire clock, doDiv, doMul, enablesA, enablesB, loadReg, memWrite, not_1_out, R1, R2;
  wire [1:0] opCode;
  wire [3:0] Avalue, Bvalue, demultiplexer_2_out0, demultiplexer_2_out1, divider_1_out, divider_1_rem,
       inmediate, multiplexer_2_out, multiplexer_3_out, multiplier_1_cout, multiplier_1_out, PC_q, ram_1_data;

  Clock clock_1 (.out(clock));
  Counter #(.width(4), .max('hf)) PC (.Q(PC_q), .clk(clock));  // open: load, D, count, carry, clr, preset, down
  ROM #(.addrWidth(4), .Select("low")) rom_1 (.addr(PC_q), .data({opCode, R1, R2, inmediate}));
  not not_1 (not_1_out, memWrite);
  Decoder #(.select(2), .enable("false")) decoder_1 (
    .out0(doMul), .out1(doDiv), .out2(loadReg), .out3(memWrite), .sel(opCode));
  RAM #(.addrWidth(4), .dataWidth(4), .Select("low")) ram_1 (
    .addr(inmediate), .data(ram_1_data), .sel(not_1_out), .clk(clock), .ld(in_1));  // open: clr
  Multiplexer #(.width(4), .enable("false")) multiplexer_1 (.in0(Avalue), .in1(Bvalue), .out(ram_1_data), .sel(R1));
  Multiplexer #(.width(4), .enable("false")) multiplexer_2 (
    .in0(Avalue), .in1(Bvalue), .out(multiplexer_2_out), .sel(R1));
  Multiplexer #(.width(4), .enable("false")) multiplexer_3 (
    .in0(Avalue), .in1(Bvalue), .out(multiplexer_3_out), .sel(R2));
  Demultiplexer #(.enable("false")) demultiplexer_1 (.out0(enablesA), .out1(enablesB), .in(loadReg), .sel(R1));
  Multiplier #(.width(4)) multiplier_1 (
    .a(multiplexer_2_out), .b(multiplexer_3_out), .out(multiplier_1_out), .cout(multiplier_1_cout));  // open: cin
  Divider #(.width(4)) divider_1 (
    .a(multiplexer_2_out), .b(multiplexer_3_out), .out(divider_1_out), .rem(divider_1_rem));  // open: upper
  Demultiplexer #(.width(4), .enable("false")) demultiplexer_2 (
    .out0(demultiplexer_2_out0), .out1(demultiplexer_2_out1), .in(inmediate), .sel(R1));
  Register #(.width(4), .Select("low")) A (
    .D(demultiplexer_2_out0), .en(enablesA), .Q(Avalue), .clk(clock));  // open: clr
  Register #(.width(4), .Select("low")) B (
    .D(demultiplexer_2_out1), .en(enablesB), .Q(Bvalue), .clk(clock));  // open: clr
  Register #(.Select("low")) P (.D({multiplier_1_cout, multiplier_1_out}), .en(doMul), .clk(clock));  // open: Q, clr
  Register #(.width(4), .Select("low")) C (.D(divider_1_out), .en(doDiv), .clk(clock));  // open: Q, clr
  Register #(.width(4), .Select("low")) R (.D(divider_1_rem), .en(doDiv), .clk(clock));  // open: Q, clr

  // Notes on the sheet:
  //   contents of rom_1 (hex, n*v repeats v):
  //   82 aa 10 60 c0 e1
  //   loadi  |  R1   |       |  10$  10    |  0     |  0   | 0010 = 82
  //   loadi  |  R1   |        |  2$  10    |  1      |  0   | 1010 = AA
  //   mul   |  R1   |   R2   |  0000$  00   |    0    |     1   | 0000 = 10
  //   div   |  R1    |   R2   |  0000$  01  |    1    |     0   |   0000 = 60
  //   store  |  R1    |      |  0000$  11    |    0     |  0  |   0000 = C0
  //   store  |  R1    |      |  0000$  11    |    1     |  0  |   0001 = E1
endmodule
